// Logisim project 4 Bit ripple carry adder circuit.circ as structural Verilog: 1 circuit, main circuit main
module main (
  input  in_1,
  input  in_2,
  input  in_3,
  input  in_4,
  input  in_5,
  input  in_6,
  input  in_7,
  input  in_8,
  input  Cin,
  output Cout,
  output out_11,
  output out_12,
  output out_13,
  output out_14
);

  wire main_1_p2, main_1_p7, main_2_p5, main_3_p5;

  // full_adder_main main_1: pin names not known; wires that end beside it: Cout, main_1_p2, main_1_p2, in_1, out_11, in_2, main_1_p7
  // full_adder_main main_2: pin names not known; wires that end beside it: main_1_p7, in_3, out_12, in_4, main_2_p5
  // full_adder_main main_3: pin names not known; wires that end beside it: main_2_p5, in_5, out_13, in_6, main_3_p5
  // full_adder_main main_4: pin names not known; wires that end beside it: main_3_p5, in_7, out_14, in_8, Cin

  // Notes on the sheet:
  //   B3
  //   A3
  //   S4
  //   C2
  //   B2
  //   A2
  //   S3
  //   C1
  //   B1
  //   A1
  //   S1
  //   C0
  //   B0
  //   A0
  //   S0
endmodule
