// Logisim project 4BitRippleCarryAdder.circ as structural Verilog: 1 circuit, main circuit main
module main (
  input  B3,
  input  A3,
  input  B2,
  input  A2,
  input  B1,
  input  A1,
  input  B0,
  input  A0,
  input  Cin,
  output Cout,
  output S4,
  output S3,
  output S2,
  output S1
);

  wire main_2_p3, main_2_p8, main_4_p3;

  // FullAdder_main main_1: pin names not known; wires that end beside it: S4, Cout
  // FullAdder_main main_2: pin names not known; wires that end beside it: A3, B3, main_2_p3, S3, main_2_p3, A2, B2, main_2_p8
  // FullAdder_main main_3: pin names not known; wires that end beside it: S2, main_2_p8
  // FullAdder_main main_4: pin names not known; wires that end beside it: A1, B1, main_4_p3, S1, main_4_p3, A0, B0, Cin

  // Notes on the sheet:
  //   Full Adder 4
  //   Full Adder 3
  //   Full Adder 2
  //   Full Adder 1
endmodule
