// Logisim project Jayasree Bhattacharya, CSE, Sec A, Roll 5, 4 Bit Arithmetic Unit.circ as structural Verilog: 1 circuit, main circuit main
module main (
  input  [1:0] S0_S1,
  input  Cin,
  input  B0,
  input  in_4,
  input  A0,
  input  B1,
  input  A1,
  input  in_8,
  input  B2,
  input  A2,
  input  in_11,
  input  A3,
  input  B3,
  input  in_14,
  output R0,
  output R1,
  output R2,
  output R3,
  output Cout
);

  wire multiplexer_1_out, multiplexer_2_out, multiplexer_3_out, multiplexer_4_out, not_1_out, not_2_out,
       not_3_out, not_4_out;

  not not_1 (not_1_out, B0);
  not not_2 (not_2_out, B1);
  not not_3 (not_3_out, B2);
  not not_4 (not_4_out, B3);
  Multiplexer #(.select(2)) multiplexer_1 (
    .in0(B0), .in1(not_1_out), .in2(1'b1), .in3(in_4), .out(multiplexer_1_out), .sel(S0_S1), .en(1'b1));
  Multiplexer #(.select(2)) multiplexer_2 (
    .in0(B1), .in1(not_2_out), .in2(1'b1), .in3(in_8), .out(multiplexer_2_out), .sel(S0_S1), .en(1'b1));
  Multiplexer #(.select(2)) multiplexer_3 (
    .in0(B2), .in1(not_3_out), .in2(1'b1), .in3(in_11), .out(multiplexer_3_out), .sel(S0_S1), .en(1'b1));
  Multiplexer #(.select(2)) multiplexer_4 (
    .in0(B3), .in1(not_4_out), .in2(1'b1), .in3(in_14), .out(multiplexer_4_out), .sel(S0_S1), .en(1'b1));
  // Raima_Sen_A_CSE_57_Four_bit_ripple_carry_adder_main main_1: pin names not known; wires that end beside it: A0, multiplexer_1_out, A1, multiplexer_2_out, A2, multiplexer_3_out, A3, multiplexer_4_out, Cin, R0, R1, R2, R3, Cout

  // Notes on the sheet:
  //   E
  //   Y0
  //   Y1
  //   Y2
  //   Y3
  //   4 BIT ARITHMETIC UNIT
endmodule
