// Logisim project LA Circuit.circ 2.circ as structural Verilog: 1 circuit, main circuit main
module main (
  input  A,
  input  B,
  input  Ci,
  output out_4,
  output Si,
  output Gi
);

  xor xor_1 (out_4, A, B);
  and and_1 (Gi, A, B);
  xor xor_2 (Si, out_4, Ci);

  // Notes on the sheet:
  //   LA Circuit
  //   Pi
endmodule
